# Fritzing sketch living-room (saved by Fritzing 0.9.6b)
breadboards: 2

parts:
  U1 = ESP32-38PinWide [part_number=ESP32-38PinWide]
  TD-er1 = MH-Z19 CO2 sensor [part_number=MH-Z19]
  Part1 = BME280

nets:
  N1: U1.3.3, Part1.VIN
  N2: U1.GPIO32, Part1.SCL
  N3: U1.GPIO33, Part1.SDA
  GND: U1.GND, TD-er1.GND, Part1.GND
  VIN: U1.VIN, TD-er1.Vin
  N4: U1.GPIO22, TD-er1.RX
  N5: U1.GPIO23, TD-er1.TX

custom parts:
  ESP32-38PinWide: Generic 38-Pin ESP32 with wide format (only access to one side of pins on a breadboard) based on Stephen Lilley's HiLetgo ESP-WROOM-32 ESP32 ESP-32S Development Board.
