# Fritzing sketch office (saved by Fritzing 0.9.6b)
breadboards: 1

parts:
  U1 = ESP32-38PinWide [part_number=ESP32-38PinWide]
  Part1 = BME280
  TD-er1 = MH-Z19 CO2 sensor [part_number=MH-Z19]

nets:
  N1: U1.3.3, Part1.VIN
  N2: U1.GPIO32, Part1.SDA
  N3: U1.GPIO33, Part1.SCL
  N4: U1.GPIO25, U1.GPIO18, TD-er1.TX
  N5: U1.GPIO26, U1.GPIO5, TD-er1.RX
  GND: U1.GND, Part1.GND, TD-er1.HD

custom parts:
  ESP32-38PinWide: Generic 38-Pin ESP32 with wide format (only access to one side of pins on a breadboard) based on Stephen Lilley's HiLetgo ESP-WROOM-32 ESP32 ESP-32S Development Board.
